// Logisim project NAND2Tetris_logisim.circ as structural Verilog: 10 circuits, main circuit main
module main (
);
endmodule

module Mux4Way16 (
  input  [15:0] a16,
  input  [15:0] b16,
  input  [15:0] c16,
  input  [15:0] d16,
  input  [1:0] sel2,
  output [15:0] out16
);

  wire [15:0] multiplexer_1_out, multiplexer_2_out;

  Multiplexer #(.width(16), .enable("false")) multiplexer_1 (
    .in0(a16), .in1(b16), .out(multiplexer_1_out), .sel(sel2[0]));
  Multiplexer #(.width(16), .enable("false")) multiplexer_2 (
    .in0(c16), .in1(d16), .out(multiplexer_2_out), .sel(sel2[0]));
  Multiplexer #(.width(16), .enable("false")) multiplexer_3 (
    .in0(multiplexer_1_out), .in1(multiplexer_2_out), .out(out16), .sel(sel2[1]));
endmodule

module Mux8Way16 (
  input  [15:0] a16,
  input  [15:0] b16,
  input  [15:0] c16,
  input  [15:0] d16,
  input  [15:0] e16,
  input  [15:0] f16,
  input  [15:0] g16,
  input  [15:0] h16,
  input  [2:0] sel3,
  output [15:0] out16
);

  wire [15:0] mux4way16_1_out16, mux4way16_2_out16;

  Mux4Way16 mux4way16_1 (.a16(a16), .b16(b16), .c16(c16), .d16(d16), .sel2(sel3[1:0]), .out16(mux4way16_1_out16));
  Mux4Way16 mux4way16_2 (.a16(e16), .b16(f16), .c16(g16), .d16(h16), .sel2(sel3[1:0]), .out16(mux4way16_2_out16));
  Multiplexer #(.width(16), .enable("false")) multiplexer_1 (
    .in0(mux4way16_1_out16), .in1(mux4way16_2_out16), .out(out16), .sel(sel3[2]));
endmodule

module Or8Way (
  input  [7:0] in8,
  output out1
);

  wire or_1_out, or_2_out, or_3_out, or_4_out, or_5_out, or_6_out;

  or or_1 (or_1_out, in8[0], in8[1]);
  or or_2 (or_2_out, in8[2], in8[3]);
  or or_3 (or_3_out, in8[4], in8[5]);
  or or_4 (or_4_out, in8[6], in8[7]);
  or or_5 (or_5_out, or_1_out, or_2_out);
  or or_6 (or_6_out, or_3_out, or_4_out);
  or or_7 (out1, or_5_out, or_6_out);
endmodule

module DMux4Way (
  input  in1,
  input  [1:0] sel2,
  output a1,
  output b1,
  output c1,
  output d1
);

  wire demultiplexer_1_out0, demultiplexer_1_out1;

  Demultiplexer #(.enable("false")) demultiplexer_1 (
    .out0(demultiplexer_1_out0), .out1(demultiplexer_1_out1), .in(in1), .sel(sel2[1]));
  Demultiplexer #(.enable("false")) demultiplexer_2 (.out0(a1), .out1(b1), .in(demultiplexer_1_out0), .sel(sel2[0]));
  Demultiplexer #(.enable("false")) demultiplexer_3 (.out0(c1), .out1(d1), .in(demultiplexer_1_out1), .sel(sel2[0]));
endmodule

module DMux8Way (
  input  in1,
  input  [2:0] sel3,
  output a1,
  output b1,
  output c1,
  output d1,
  output e1,
  output f1,
  output g1,
  output h1
);

  wire demultiplexer_1_out0, demultiplexer_1_out1;

  Demultiplexer #(.enable("false")) demultiplexer_1 (
    .out0(demultiplexer_1_out0), .out1(demultiplexer_1_out1), .in(in1), .sel(sel3[2]));
  DMux4Way dmux4way_1 (.in1(demultiplexer_1_out0), .sel2(sel3[1:0]), .a1(a1), .b1(b1), .c1(c1), .d1(d1));
  DMux4Way dmux4way_2 (.in1(demultiplexer_1_out1), .sel2(sel3[1:0]), .a1(e1), .b1(f1), .c1(g1), .d1(h1));
endmodule

module HalfAdder (
  input  a,
  input  b,
  output sum,
  output carry
);

  xor xor_1 (sum, a, b);
  and and_1 (carry, a, b);
endmodule

module FullAdder (
  input  a,
  input  b,
  input  c,
  output sum,
  output carry
);

  wire halfadder_1_carry, halfadder_1_sum, halfadder_2_carry;

  HalfAdder halfadder_1 (.a(a), .b(b), .sum(halfadder_1_sum), .carry(halfadder_1_carry));
  HalfAdder halfadder_2 (.a(halfadder_1_sum), .b(c), .sum(sum), .carry(halfadder_2_carry));
  xor xor_1 (carry, halfadder_2_carry, halfadder_1_carry);
endmodule

module Add16 (
  input  [15:0] a16,
  input  [15:0] b16,
  output [15:0] out16
);

  wire fulladder_1_carry, fulladder_2_carry, fulladder_3_carry, fulladder_4_carry, fulladder_5_carry,
       fulladder_6_carry, fulladder_7_carry, fulladder_8_carry, fulladder_9_carry, fulladder_10_carry,
       fulladder_11_carry, fulladder_12_carry, fulladder_13_carry, fulladder_14_carry, fulladder_15_carry,
       halfadder_1_carry;

  HalfAdder halfadder_1 (.a(a16[0]), .b(b16[0]), .sum(out16[0]), .carry(halfadder_1_carry));
  FullAdder fulladder_1 (.sum(out16[1]), .b(b16[1]), .a(a16[1]), .c(halfadder_1_carry), .carry(fulladder_1_carry));
  FullAdder fulladder_2 (.sum(out16[2]), .b(b16[2]), .a(a16[2]), .c(fulladder_1_carry), .carry(fulladder_2_carry));
  FullAdder fulladder_3 (.sum(out16[3]), .b(b16[3]), .a(a16[3]), .c(fulladder_2_carry), .carry(fulladder_3_carry));
  FullAdder fulladder_4 (.sum(out16[4]), .b(b16[4]), .a(a16[4]), .c(fulladder_3_carry), .carry(fulladder_4_carry));
  FullAdder fulladder_5 (.sum(out16[5]), .b(b16[5]), .a(a16[5]), .c(fulladder_4_carry), .carry(fulladder_5_carry));
  FullAdder fulladder_6 (.sum(out16[6]), .b(b16[6]), .a(a16[6]), .c(fulladder_5_carry), .carry(fulladder_6_carry));
  FullAdder fulladder_7 (.sum(out16[7]), .b(b16[7]), .a(a16[7]), .c(fulladder_6_carry), .carry(fulladder_7_carry));
  FullAdder fulladder_8 (.sum(out16[8]), .b(b16[8]), .a(a16[8]), .c(fulladder_7_carry), .carry(fulladder_8_carry));
  FullAdder fulladder_9 (.sum(out16[9]), .b(b16[9]), .a(a16[9]), .c(fulladder_8_carry), .carry(fulladder_9_carry));
  FullAdder fulladder_10 (.sum(out16[10]), .b(b16[10]), .a(a16[10]), .c(fulladder_9_carry), .carry(fulladder_10_carry));
  FullAdder fulladder_11 (
    .sum(out16[11]), .b(b16[11]), .a(a16[11]), .c(fulladder_10_carry), .carry(fulladder_11_carry));
  FullAdder fulladder_12 (
    .sum(out16[12]), .b(b16[12]), .a(a16[12]), .c(fulladder_11_carry), .carry(fulladder_12_carry));
  FullAdder fulladder_13 (
    .sum(out16[13]), .b(b16[13]), .a(a16[13]), .c(fulladder_12_carry), .carry(fulladder_13_carry));
  FullAdder fulladder_14 (
    .sum(out16[14]), .b(b16[14]), .a(a16[14]), .c(fulladder_13_carry), .carry(fulladder_14_carry));
  FullAdder fulladder_15 (
    .sum(out16[15]), .b(b16[15]), .a(a16[15]), .c(fulladder_14_carry), .carry(fulladder_15_carry));
  LED led_1 (.in(fulladder_15_carry));
endmodule

module Inc16 (
  input  [15:0] a,
  input  in_2,
  output [15:0] out_3
);

  wire halfadder_1_carry, halfadder_2_carry, halfadder_3_carry, halfadder_4_carry, halfadder_5_carry,
       halfadder_6_carry, halfadder_7_carry, halfadder_8_carry, halfadder_9_carry, halfadder_10_carry,
       halfadder_11_carry, halfadder_12_carry, halfadder_13_carry, halfadder_14_carry, halfadder_15_carry;

  HalfAdder halfadder_1 (.a(a[0]), .b(in_2), .sum(out_3[0]), .carry(halfadder_1_carry));
  HalfAdder halfadder_2 (.a(a[1]), .b(halfadder_1_carry), .sum(out_3[1]), .carry(halfadder_2_carry));
  HalfAdder halfadder_3 (.a(a[2]), .b(halfadder_2_carry), .sum(out_3[2]), .carry(halfadder_3_carry));
  HalfAdder halfadder_4 (.a(a[3]), .b(halfadder_3_carry), .sum(out_3[3]), .carry(halfadder_4_carry));
  HalfAdder halfadder_5 (.a(a[4]), .b(halfadder_4_carry), .sum(out_3[4]), .carry(halfadder_5_carry));
  HalfAdder halfadder_6 (.a(a[5]), .b(halfadder_5_carry), .sum(out_3[5]), .carry(halfadder_6_carry));
  HalfAdder halfadder_7 (.a(a[6]), .b(halfadder_6_carry), .sum(out_3[6]), .carry(halfadder_7_carry));
  HalfAdder halfadder_8 (.a(a[7]), .b(halfadder_7_carry), .sum(out_3[7]), .carry(halfadder_8_carry));
  HalfAdder halfadder_9 (.a(a[8]), .b(halfadder_8_carry), .sum(out_3[8]), .carry(halfadder_9_carry));
  HalfAdder halfadder_10 (.a(a[9]), .b(halfadder_9_carry), .sum(out_3[9]), .carry(halfadder_10_carry));
  HalfAdder halfadder_11 (.a(a[10]), .b(halfadder_10_carry), .sum(out_3[10]), .carry(halfadder_11_carry));
  HalfAdder halfadder_12 (.a(a[11]), .b(halfadder_11_carry), .sum(out_3[11]), .carry(halfadder_12_carry));
  HalfAdder halfadder_13 (.a(a[12]), .b(halfadder_12_carry), .sum(out_3[12]), .carry(halfadder_13_carry));
  HalfAdder halfadder_14 (.a(a[13]), .b(halfadder_13_carry), .sum(out_3[13]), .carry(halfadder_14_carry));
  HalfAdder halfadder_15 (.a(a[14]), .b(halfadder_14_carry), .sum(out_3[14]), .carry(halfadder_15_carry));
  HalfAdder halfadder_16 (.a(a[15]), .b(halfadder_15_carry), .sum(out_3[15]));  // open: carry
endmodule
